# Fritzing sketch WDI Fritzing (saved by Fritzing 0.9.3b)
perfboards: 1

parts:
  U3 = NodeMCU V3.0
  Power_plug2 = Power plug
  Q5 = npn-Powertransistor [package="TO220 [THT]"]
  R6 = Resistor [tolerance=±5% resistance=220 package="2512 [SMD]"]
  Q6 = npn-Powertransistor [package="TO220 [THT]"]
  R7 = Resistor [tolerance=±5% resistance=220 package="2512 [SMD]"]
  Q7 = npn-Powertransistor [package="TO220 [THT]"]
  Q8 = npn-Powertransistor [package="TO220 [THT]"]
  R8 = Resistor [tolerance=±5% resistance=220 package="2512 [SMD]"]
  R9 = Resistor [tolerance=±5% resistance=220 package="2512 [SMD]"]
  IC1 = Voltage Regulator [package=to220-igo]

nets:
  N1: U3.D0, R9.Pin_1
  N2: U3.D2, R8.Pin_1
  N3: U3.GND#6, U3.GND#13, U3.GND#16, U3.GND#33
  N4: U3.D5, R7.Pin_1
  N5: U3.D8, R6.Pin_1
  N6: U3.Vin, IC1.OUT
  N7: Power_plug2.GND, Q5.emitter
  N8: Q6.base, R7.Pin_0
  N9: Q7.base, R8.Pin_0
  N10: Q8.base, R9.Pin_0

notes:
  <------ 5V
  12V ----->

custom parts:
  NodeMCU V3.0: ESP8266 based NodeMCU
